# Fritzing sketch motorCircuit (saved by Fritzing 0.9.3b)
breadboards: 1

parts:
  Motor_Circuit = Rotoshield - Motor driver shield for Arduino
  Cake_Clock_Motor = Stepper Motor - Bipolar
  Rotary_Motor = Stepper Motor - Bipolar

nets:
  N1: Motor_Circuit.M1-2, Cake_Clock_Motor.D
  N2: Motor_Circuit.M1-1, Cake_Clock_Motor.B
  N3: Motor_Circuit.M2-2, Cake_Clock_Motor.C
  N4: Motor_Circuit.M2-1, Cake_Clock_Motor.A
  N5: Motor_Circuit.M3-2, Rotary_Motor.D
  N6: Motor_Circuit.M3-1, Rotary_Motor.B
  N7: Motor_Circuit.M4-2, Rotary_Motor.C
  N8: Motor_Circuit.M4-1, Rotary_Motor.A
