# Fritzing sketch sensorsCircuit (saved by Fritzing 0.9.3b)
breadboards: 1

parts:
  Bottom_Clock_Arduino_Sensors_Circuit = Arduino Uno (Rev3)
  part = Resistor [tolerance=±5% resistance=500 package=THT]
  Force_Sensor = Basic Force Sensing Resistor (FSR) [package=THT]
  Distance_Sensor_3 = Infrared Proximity Sensor
  Distance_Sensor_2 = Infrared Proximity Sensor
  Distance_Sensor_1 = Infrared Proximity Sensor
  IR1 = PHOTOTRANSISTOR REFLECTIVE OBJECT SENSOR [package=qrb1114-side]
  IR2 = PHOTOTRANSISTOR REFLECTIVE OBJECT SENSOR [package=qrb1114-side]
  IR3 = PHOTOTRANSISTOR REFLECTIVE OBJECT SENSOR [package=qrb1114-side]
  IR4 = PHOTOTRANSISTOR REFLECTIVE OBJECT SENSOR [package=qrb1114-side]
  Sensor_LED_Strip = Luxeon LED [package=luxeon]
  Animal_LED_Strip = Luxeon LED [package=luxeon]
  part_2 = Resistor [tolerance=±5% resistance=365 package=THT]
  part_3 = Resistor [tolerance=±5% resistance=365 package=THT]
  part_4 = Resistor [tolerance=±5% resistance=800 package=THT]
  part_5 = Resistor [tolerance=±5% resistance=800 package=THT]
  part_6 = Resistor [tolerance=±5% resistance=800 package=THT]
  part_7 = Resistor [tolerance=±5% resistance=800 package=THT]
  part_8 = Resistor [tolerance=±5% resistance=2k package=THT]
  part_9 = Resistor [tolerance=±5% resistance=2k package=THT]
  part_10 = Resistor [tolerance=±5% resistance=2k package=THT]
  part_11 = Resistor [tolerance=±5% resistance=2k package=THT]
  Light_House_Servo = Basic Servo
  Light_House_LED = Luxeon LED [package=luxeon]
  part_12 = Resistor [tolerance=±5% resistance=365 package=THT]

nets:
  N1: Bottom_Clock_Arduino_Sensors_Circuit.A0, Distance_Sensor_1.Vout
  N2: Bottom_Clock_Arduino_Sensors_Circuit.A1, Distance_Sensor_2.Vout
  N3: Bottom_Clock_Arduino_Sensors_Circuit.A2, Distance_Sensor_3.Vout
  N4: Bottom_Clock_Arduino_Sensors_Circuit.A4/SDA, part.Pin_1
  N5: Bottom_Clock_Arduino_Sensors_Circuit.D8, part_4.Pin_1
  N6: Bottom_Clock_Arduino_Sensors_Circuit.D9_PWM, part_5.Pin_1
  N7: Bottom_Clock_Arduino_Sensors_Circuit.D10_PWM/SS, part_6.Pin_1
  N8: Bottom_Clock_Arduino_Sensors_Circuit.D11_PWM/MOSI, Light_House_Servo.pulse
  GND: Bottom_Clock_Arduino_Sensors_Circuit.GND, Distance_Sensor_3.GND, Distance_Sensor_2.GND, Distance_Sensor_1.GND, IR1.E, IR1.K, IR2.E, IR2.K, IR3.E, IR3.K, IR4.E, IR4.K, Sensor_LED_Strip.C, Animal_LED_Strip.C, Light_House_Servo.gnd, Light_House_LED.C
  N9: Bottom_Clock_Arduino_Sensors_Circuit.D3_PWM, part_12.Pin_0
  N10: Bottom_Clock_Arduino_Sensors_Circuit.D7, part_7.Pin_1
  VCC: Bottom_Clock_Arduino_Sensors_Circuit.5V, Force_Sensor.pin_0, Distance_Sensor_3.Vcc, Distance_Sensor_2.Vcc, Distance_Sensor_1.Vcc, Sensor_LED_Strip.A, Animal_LED_Strip.A, part_4.Pin_0, part_5.Pin_0, part_6.Pin_0, part_7.Pin_0, part_8.Pin_0, part_9.Pin_0, part_10.Pin_0, part_11.Pin_0, Light_House_Servo.vcc, Light_House_LED.A
  N11: part.Pin_0, Force_Sensor.pin_1
  N12: Sensor_LED_Strip.S, part_2.Pin_1
  N13: Animal_LED_Strip.S, part_3.Pin_1
  N14: Light_House_LED.S, part_12.Pin_1
